// Digital circuit Lab00b.dig as structural Verilog
module Lab00b (
);

  wire led1_p2, switch1_b;

  Switch switch1 (.A(1'b1), .B(switch1_b));
  // PolarityAwareLED led1: pin names not known; wires that end beside it: switch1_b, led1_p2
  Switch switch2 (.A(led1_p2), .B(1'b0));
endmodule
